// Logisim project ARI01.circ as structural Verilog: 2 circuits, main circuit main
module main (
  input  P10,
  input  P5,
  input  P6,
  input  P16,
  input  P11,
  input  P7,
  input  P21,
  input  P8,
  input  P12,
  input  P20,
  input  P13,
  input  P39,
  input  P37,
  input  P38,
  input  P35,
  input  P36,
  input  P33,
  input  P34,
  input  P31,
  input  P25,
  input  P32,
  input  P28,
  input  P29,
  input  P30,
  input  P18,
  input  P17,
  output P19,
  output P23,
  output P30_2
);

  wire and_1_out, Q4_out, Q5_out, Q6_out, Q7_out, Q15_out, Q16_out, Q17_out, Q18_out, Q19_out, Q20_out,
       Q21_out, Q22_out, Q23_out, Q24_out;

  nand Q1 (P39, P5, P6);
  nand Q2 (P39, P7, P8);
  Pull_Resistor #(.pull(1)) pull_resistor_1 (.node(P39));
  not Q3 (P16, P39);
  nand Q19 (Q19_out, P39, P37, P38);
  nand Q18 (Q18_out, P35, P36);
  nand Q17 (Q17_out, P33, P34);
  nand Q16 (Q16_out, P31, P32);
  nand Q15 (Q15_out, P28, P29, P30);
  Pull_Resistor #(.pull(1)) pull_resistor_2 (.node(P16));
  nand Q5 (Q5_out, P11, P39);
  nand Q6 (Q6_out, P12, P13);
  nand Q4 (Q4_out, P10, P16);
  not Q10 (P23, P25);
  nand Q11 (P25, Q19_out, Q18_out, Q17_out, Q16_out, Q15_out);
  and and_1 (and_1_out, Q4_out, Q5_out, Q6_out);
  not Q7 (Q7_out, and_1_out);
  not Q20 (Q20_out, P38);
  nand Q21 (Q21_out, P38, P17, and_1_out);
  nand Q22 (Q22_out, Q7_out, P17, Q20_out);
  nand Q23 (Q23_out, Q7_out, P38, P18);
  nand Q24 (Q24_out, Q20_out, and_1_out, P18);
  Pull_Resistor #(.pull(1)) pull_resistor_3 (.node(P20));
  nand Q14 (P20, Q7_out, P18);
  nand Q13 (P20, P18, P38);
  nand Q9 (P20, P21, P38, Q7_out);
  nand Q12 (P30_2, Q21_out, Q22_out, Q23_out, Q24_out);
  not Q8 (P19, P20);

  // Notes on the sheet:
  //   Q1 drives only 0 and floats otherwise
  //   Q2 drives only 0 and floats otherwise
  //   Q3 drives only 0 and floats otherwise
  //   Q10 drives only 0 and floats otherwise
  //   Q14 drives only 0 and floats otherwise
  //   Q13 drives only 0 and floats otherwise
  //   Q9 drives only 0 and floats otherwise
endmodule

module main_aggressive (
  input  P5,
  input  P21,
  input  P6,
  input  P10,
  input  P7,
  input  P11,
  input  P8,
  input  P12,
  input  P13,
  input  P37,
  input  P38,
  input  P35,
  input  P36,
  input  P33,
  input  P34,
  input  P31,
  input  P32,
  input  P28,
  input  P29,
  input  P30,
  input  P18,
  input  P17,
  output P19,
  output P20,
  output P16,
  output P39,
  output P25,
  output P23,
  output P30_2
);

  wire multiplexer_1_out, not_1_out, not_2_out, Q1_out, Q2_out, Q6_out, Q7_out, Q9_out, Q13_out, Q14_out,
       Q15_out, Q16_out, Q17_out, Q18_out, Q19_out;

  nand Q1 (Q1_out, P5, P6);
  and and_1 (P39, Q1_out, Q2_out);
  nand Q2 (Q2_out, P7, P8);
  not Q3 (P16, P39);
  nand Q19 (Q19_out, P39, P37, P38);
  nand Q18 (Q18_out, P35, P36);
  nand Q17 (Q17_out, P33, P34);
  nand Q16 (Q16_out, P31, P32);
  nand Q15 (Q15_out, P28, P29, P30);
  not not_1 (not_1_out, P10);
  not not_2 (not_2_out, P11);
  nand Q6 (Q6_out, P12, P13);
  nand Q11 (P25, Q19_out, Q18_out, Q17_out, Q16_out, Q15_out);
  Multiplexer #(.disabled(0)) multiplexer_1 (
    .in0(not_1_out), .in1(not_2_out), .out(multiplexer_1_out), .sel(P39), .en(Q6_out));
  not Q10 (P23, P25);
  not Q7 (Q7_out, multiplexer_1_out);
  nand Q14 (Q14_out, Q7_out, P18);
  nand Q13 (Q13_out, P18, P38);
  nand Q9 (Q9_out, P21, P38, Q7_out);
  and and_2 (P20, Q14_out, Q13_out, Q9_out);
  NotExactlyOne xnor_1 (.out(P30_2), .in0(Q7_out), .in1(P38), .in2(P18));
  not Q8 (P19, P20);

  // Notes on the sheet:
  //   R Register
  //   "Selects" the bitwise portion in some way?
  //   Decoding logic of some flavor
  //   I suspect that most of the function here is "programmed" by the backplane
  //   If P12 and P13 are set, second input is ignored
  //   Bitwise, probably? very generic
  //   Q10 drives only 0 and floats otherwise
  //   CarryIn
  //   ~CarryIn
  //   Internally both are used to save gates, I'm just simplifying that out here
  //   I'm a little unsure why P21 is here
  //   CarryOut
  //   ~CarryOut
  //   Sum
endmodule
